# Fritzing sketch Untitled Sketch (saved by Fritzing 0.9.3b)
circuit board: 8.46667cm x 5.64444cm
breadboards: 1

parts:
  Часть1 = Arduino Uno (Rev3)
  R1 = Resistor [tolerance=±5% resistance=220 package=THT]
  S1 = Pushbutton [package="[THT]"]
  S2 = Pushbutton [package="[THT]"]
  S3 = Pushbutton [package="[THT]"]
  R2 = Resistor [tolerance=±5% resistance=220 package=THT]
  R3 = Resistor [tolerance=±5% resistance=220 package=THT]
  R5 = Resistor [tolerance=±5% resistance=220 package=THT]
  R6 = Resistor [tolerance=±5% resistance=220 package=THT]
  R7 = Resistor [tolerance=±5% resistance=220 package=THT]
  LED1 = LED - 5mm [color="Red (633nm)" package="5 mm [THT]"]
  LED2 = LED - 5mm [color="Red (633nm)" package="5 mm [THT]"]
  LED3 = LED - 5mm [color="Red (633nm)" package="5 mm [THT]"]

nets:
  N1: Часть1.A0, R1.Pin_1, S1.Pin_3, S1.Pin_4
  N2: Часть1.A1, S2.Pin_3, S2.Pin_4, R2.Pin_1
  N3: Часть1.A2, S3.Pin_3, S3.Pin_4, R3.Pin_1
  N4: Часть1.GND, R5.Pin_1, R6.Pin_1, R7.Pin_1
  N5: Часть1.D4, LED1.anode
  N6: Часть1.D5_PWM, LED2.anode
  N7: Часть1.D6_PWM, LED3.anode
  N8: Часть1.5V, R1.Pin_0, S1.Pin_1, S1.Pin_2, S2.Pin_1, S2.Pin_2, S3.Pin_1, S3.Pin_2, R2.Pin_0, R3.Pin_0
  N9: R5.Pin_0, LED2.cathode
  N10: R6.Pin_0, LED3.cathode
  N11: R7.Pin_0, LED1.cathode
