# Fritzing sketch 5 (saved by Fritzing 0.9.3b)
breadboards: 1

parts:
  Часть1 = Arduino Uno (Rev3)
  LCD1 = LCD screen
  C1 = Electrolytic Capacitor [capacitance=1µF package="100 mil [THT, electrolytic]"]
  R1 = Resistor [tolerance=±5% resistance=220 package=THT]
  R2 = Resistor [tolerance=±5% resistance=10k package=THT]

nets (from the schematic view):
  N1: Часть1.A0, C1.+, R1.Pin_0, R2.Pin_1
  N2: Часть1.D8, LCD1.DB6
  N3: Часть1.D9_PWM, LCD1.DB5
  N4: Часть1.D10_PWM/SS, LCD1.E
  N5: Часть1.D11_PWM/MOSI, R1.Pin_1
  N6: Часть1.D13/SCK, R2.Pin_0
  N7: Часть1.GND, LCD1.DB0, C1.-
  N8: Часть1.D5_PWM, LCD1.LED-
  N9: Часть1.D6_PWM, LCD1.LED+
  N10: Часть1.D7, LCD1.DB7
  5V: Часть1.5V, LCD1.VSS
  N11: LCD1.VDD, LCD1.R/W
